# Fritzing sketch AmplifierLM386 (saved by Fritzing 0.9.3b)
breadboards: 1

parts:
  LM386 = LM386 [package=dip08]
  C1 = Electrolytic Capacitor [capacitance=999µF package="100 mil [THT, electrolytic]"]
  8O_speaker = Loudspeaker
  VCC1 = Battery block 9V
  C2 = Electrolytic Capacitor [capacitance=100µF package="100 mil [THT, electrolytic]"]
  C3 = Electrolytic Capacitor [capacitance=100µF package="100 mil [THT, electrolytic]"]
  C4 = Ceramic Capacitor [capacitance=100nF package="100 mil [THT, multilayer]"]

nets:
  GND: LM386.-IN, LM386.V-, 8O_speaker.pin2, VCC1.-, C2.-, C3.-, C4.0
  input: LM386.+IN
  N1: LM386.OUT, C1.+, C4.1
  N2: LM386.V+, VCC1.+, C2.+
  N3: LM386.BP, C3.+
  N4: C1.-, 8O_speaker.pin1
