# Fritzing sketch ArduinoBreadboard (saved by Fritzing 0.9.3b)
breadboards: 1

parts:
  U1 = Voltage Regulator - 5V [package="TO220 [THT]"]
  U2 = atmega328 [package=dip]
  XTAL1 = Crystal [frequency="16 Mhz" package=THT]
  C1 = Ceramic Capacitor [capacitance=22pF package="100 mil [THT, multilayer]"]
  C2 = Ceramic Capacitor [capacitance=22pF package="100 mil [THT, multilayer]"]
  R1 = Resistor [tolerance=±5% resistance=10k package=THT]
  C3 = Electrolytic Capacitor [capacitance=10µF package="100 mil [THT, electrolytic]"]
  C4 = Electrolytic Capacitor [capacitance=10µF package="100 mil [THT, electrolytic]"]

nets:
  N1: U1.input_voltage, C4.+
  GND/gnd: U1.GND, U2.GND, C1.1, C2.1, C3.-, C4.-
  vcc: U1.output_voltage, U2.VCC, U2.AVCC, U2.AREF, R1.Pin_0, C3.+
  N2: U2.RESET, R1.Pin_1
  N3: U2.XLAT1, XTAL1.pin_0, C1.0
  N4: U2.XLAT2, XTAL1.pin_1, C2.0
