# Fritzing sketch LM386-Huidig (saved by Fritzing 0.9.3b)
breadboards: 1

parts:
  VCC1 = Battery block 9V
  C1 = Electrolytic Capacitor [capacitance=999µF package="100 mil [THT, electrolytic]"]
  LM386 = LM386 [package=dip08]
  C2 = Ceramic Capacitor [capacitance=100nF package="100 mil [THT, multilayer]"]
  R1 = Resistor [tolerance=±5% resistance=10 package=THT]
  SPKR1 = Loudspeaker
  C3 = Electrolytic Capacitor [capacitance=220µF package="100 mil [THT, electrolytic]"]
  R2 = Rotary Potentiometer (Small) [maximum_resistance=10kΩ package=THT]
  C5 = Ceramic Capacitor [capacitance=10nF package="100 mil [THT, multilayer]"]
  C4 = Ceramic Capacitor [capacitance=220nF package="100 mil [THT, multilayer]"]
  R3 = Resistor [tolerance=±5% resistance=330 package=THT]

nets:
  N1: VCC1.-, C1.-, LM386.-IN, LM386.V-, R1.Pin_1, SPKR1.pin1, R2.leg1, C5.1
  N2: VCC1.+, C1.+, LM386.V+
  N3: LM386.+IN, R2.wiper
  N4: LM386.OUT, C2.0, C3.+
  N5: C2.1, R1.Pin_0
  N6: SPKR1.pin2, C3.-
  N7: R2.leg2, C4.0
  N8: C5.0, C4.1, R3.Pin_0
