# Fritzing sketch OpAmp-virtual-ground-Full-Circuit (saved by Fritzing 0.9.3b)
breadboards: 1

parts:
  VCC1 = Battery block 9V
  R1 = Resistor [tolerance=±5% resistance=100k package=THT]
  R2 = Resistor [tolerance=±5% resistance=100k package=THT]
  TL072 = Dual Op-Amp [package=dip08]
  C1 = Electrolytic Capacitor [capacitance=470µF package="100 mil [THT, electrolytic]"]
  IC1 = IC, DIP package, 20 pins [chip_label=IC]
  R3 = Resistor [tolerance=±5% resistance=10 package=THT]
  R5 = Resistor [tolerance=±5% resistance=620 package=THT]
  R4 = Resistor [tolerance=±5% resistance=4.7k package=THT]
  C2 = Ceramic Capacitor [capacitance=470pF package="100 mil [THT, multilayer]"]
  R6 = Resistor [tolerance=±5% resistance=330 package=THT]
  C3 = Ceramic Capacitor [capacitance=100nF package="100 mil [THT, multilayer]"]
  C4 = Ceramic Capacitor [capacitance=220nF package="100 mil [THT, multilayer]"]
  R7 = Rotary Potentiometer (Small) [maximum_resistance=10kΩ package=THT]
  U1 = LM386 [package=dip08]
  C5 = Ceramic Capacitor [capacitance=100nF package="100 mil [THT, multilayer]"]
  R8 = Resistor [tolerance=±5% resistance=10 package=THT]
  C6 = Electrolytic Capacitor [capacitance=470µF package="100 mil [THT, electrolytic]"]
  SPKR1 = Loudspeaker

nets:
  0V/GND/V0: VCC1.-, R2.Pin_0, TL072.A_V-, C1.-, IC1.pin5, IC1.pin6, IC1.pin15, IC1.pin16, IC1.pin20, R5.Pin_1, C2.1, C3.1, R7.leg1, U1.-IN, U1.V-, R8.Pin_1, SPKR1.pin1
  9V: VCC1.+, R1.Pin_1, TL072.A_V+, C1.+, R4.Pin_1, U1.V+
  N1: R1.Pin_0, R2.Pin_1, TL072.B_+IN
  rfb/vout: TL072.A_OUT, IC1.pin3, R6.Pin_0
  out: TL072.A_-IN, IC1.pin2
  VG: TL072.A_+IN, TL072.B_-IN, TL072.B_OUT, IC1.pin1
  ref: IC1.pin4, R3.Pin_0, C2.0
  5V: IC1.pin17
  N2: R3.Pin_1, R5.Pin_0, R4.Pin_0
  N3: R6.Pin_1, C3.0, C4.0
  N4: C4.1, R7.leg2
  N5: R7.wiper, U1.+IN
  N6: U1.OUT, C5.0, C6.+
  N7: C5.1, R8.Pin_0
  N8: C6.-, SPKR1.pin2

notes:
  ref tov VG of V0?
