# Fritzing sketch OpAmp-virtual-ground (saved by Fritzing 0.9.3b)
breadboards: 1

parts:
  VCC1 = Battery block 9V
  R1 = Resistor [tolerance=±5% resistance=100k package=THT]
  R2 = Resistor [tolerance=±5% resistance=100k package=THT]
  TL072 = Dual Op-Amp [package=dip08]
  C1 = Electrolytic Capacitor [capacitance=470µF package="100 mil [THT, electrolytic]"]

nets:
  0V/GND: VCC1.-, R2.Pin_0, TL072.A_V-, C1.-
  9V: VCC1.+, R1.Pin_1, TL072.A_V+, C1.+
  N1: R1.Pin_0, R2.Pin_1, TL072.B_+IN
  Virtual ground (4.5V): TL072.B_-IN, TL072.B_OUT
