# Fritzing sketch TotaleSchakelingDualSupplyVoltage (saved by Fritzing 0.9.3b)
breadboards: 1

parts:
  Onderdeel1 = Arduino Uno (Rev3)
  VCC1 = Battery block 9V
  VCC2 = Battery block 9V
  C1 = Electrolytic Capacitor [capacitance=2.2mF package="100 mil [THT, electrolytic]"]
  U1 = LM386 [package=dip08]
  IC2 = IC, DIP package, 8 pins [chip_label=IC]
  IC3 = IC, DIP package, 20 pins [chip_label=IC]
  C2 = Ceramic Capacitor [capacitance=100nF package="100 mil [THT, multilayer]"]
  C3 = Electrolytic Capacitor [capacitance=1mF package="100 mil [THT, electrolytic]"]
  SPKR1 = Loudspeaker
  R1 = Rotary Potentiometer (Small) [maximum_resistance=100kΩ package=THT]
  C4 = Ceramic Capacitor [capacitance=220nF package="100 mil [THT, multilayer]"]
  R2 = Resistor [tolerance=±5% resistance=330 package=THT]
  C5 = Ceramic Capacitor [capacitance=100nF package="100 mil [THT, multilayer]"]
  C6 = Electrolytic Capacitor [capacitance=1µF package="100 mil [THT, electrolytic]"]
  R3 = Resistor [tolerance=±5% resistance=4.7k package=THT]
  R4 = Resistor [tolerance=±5% resistance=620 package=THT]
  R5 = Resistor [tolerance=±5% resistance=10 package=THT]
  C7 = Ceramic Capacitor [capacitance=470pF package="100 mil [THT, multilayer]"]
  R6 = Resistor [tolerance=±5% resistance=10 package=THT]

nets:
  N1: Onderdeel1.GND, VCC1.+, VCC2.-, C1.-, U1.-IN, U1.V-, IC2.pin3, IC3.pin1, IC3.pin5, IC3.pin6, IC3.pin15, IC3.pin16, IC3.pin20, SPKR1.pin1, R1.leg1, C6.-, R4.Pin_1, C7.0, R6.Pin_1
  N2: Onderdeel1.5V, IC3.pin17
  N3: Onderdeel1.VIN, VCC2.+, C1.+, U1.V+, IC2.pin8, C6.+, R3.Pin_1
  N4: VCC1.-, IC2.pin4
  N5: U1.+IN, R1.wiper
  N6: U1.OUT, C2.0, C3.+
  N7: IC2.pin1, IC3.pin3, R2.Pin_0
  N8: IC2.pin2, IC3.pin2
  N9: IC3.pin4, R5.Pin_0, C7.1
  N10: C2.1, R6.Pin_0
  N11: C3.-, SPKR1.pin2
  N12: R1.leg2, C4.1
  N13: C4.0, R2.Pin_1, C5.0
  N14: R3.Pin_0, R4.Pin_0, R5.Pin_1
