# Fritzing sketch Virtual ground and source (saved by Fritzing 0.9.3b)
breadboards: 1

parts:
  VCC1 = Battery block 9V
  C1 = Electrolytic Capacitor [capacitance=470µF package="100 mil [THT, electrolytic]"]
  R1 = Resistor [tolerance=±5% resistance=4.7k package=THT]
  R2 = Resistor [tolerance=±5% resistance=4.7k package=THT]
  C2 = Electrolytic Capacitor [capacitance=470µF package="100 mil [THT, electrolytic]"]
  R3 = Resistor [tolerance=±5% resistance=4.7k package=THT]
  R4 = Resistor [tolerance=±5% resistance=2.2k package=THT]
  R5 = Resistor [tolerance=±5% resistance=150 package=THT]
  C3 = Electrolytic Capacitor [capacitance=470µF package="100 mil [THT, electrolytic]"]

nets:
  N1: VCC1.-, C1.-, R1.Pin_1, C2.-, R3.Pin_1, C3.-
  N2: VCC1.+, C1.+, R2.Pin_1, R4.Pin_1
  GND/virtual ground (AGND, +4.5V): R1.Pin_0, R2.Pin_0, C2.+
  Analog source (VRef, 6V): R3.Pin_0, R5.Pin_0, C3.+
  N3: R4.Pin_0, R5.Pin_1

notes:
  9V / 7.5V = 4K7 / 470K+470K
  9V / 4.5V = 4K7 / 4K7
  9V / 6V = 4K7 / 2K2 + 150K
  +9V
  0V
