# Fritzing sketch dfplayer (saved by Fritzing 0.9.3b)
circuit board: 8.46667cm x 5.64444cm
breadboards: 1

parts:
  U1 = Voltage Regulator - 5V [package="TO220 [THT]"]
  VCC1 = Battery block 9V
  C1 = Electrolytic Capacitor [capacitance=0.22mF package="100 mil [THT, electrolytic]"]
  C2 = Ceramic Capacitor [capacitance=0.1µF package="100 mil [THT, multilayer]"]
  C3 = Electrolytic Capacitor [capacitance=0.1mF package="100 mil [THT, electrolytic]"]
  C4 = Ceramic Capacitor [capacitance=0.1µF package="100 mil [THT, multilayer]"]
  DFRobot_DFPlayer_Mini1 = DFRobot DFPlayer Mini [part_number=DFR0299]
  S1 = Pushbutton [package="[THT]"]
  S2 = Pushbutton [package="[THT]"]
  D1 = Rectifier Diode [part_number=1N4001 package="300 mil [THT]"]
  VCC2 = Battery block 9V
  Power = female pin header, 2 pins [form="♀ (female)"]
  Audio = female pin header, 2 pins [form="♀ (female)"]
  U2 = POT [package=3362u]
  J2 = female pin header, 16 pins [form="♀ (female)"]  # not connected
  J1 = female pin header, 14 pins [form="♀ (female)"]  # not connected

nets:
  N1: U1.input_voltage, VCC1.+, C1.+, C2.1, VCC2.-
  N2: U1.GND, VCC1.-, C1.-, C2.0, C3.-, C4.0, DFRobot_DFPlayer_Mini1.GND-1, DFRobot_DFPlayer_Mini1.GND-2, S1.Pin_1, S1.Pin_2, S2.Pin_1, S2.Pin_2, Power.pin1, Audio.pin1, U2.A
  N3: U1.output_voltage, C3.+, C4.1, D1.anode
  N4: DFRobot_DFPlayer_Mini1.VCC, D1.cathode
  N5: DFRobot_DFPlayer_Mini1.DAC_L, U2.E
  N6: DFRobot_DFPlayer_Mini1.IO_1, S1.Pin_3, S1.Pin_4
  N7: DFRobot_DFPlayer_Mini1.IO_2, S2.Pin_3, S2.Pin_4
  N8: VCC2.+, Power.pin2
  N9: Audio.pin2, U2.S
