# Fritzing sketch 3V5V-conversie (saved by Fritzing 0.9.4)
circuit board: 8.46667cm x 5.64444cm
breadboards: 1

parts:
  IC1 = IC, DIP package, 14 pins [chip_label=74AHCT126]
  V1 = DC Power [voltage=5]
  Rpulldown = Resistor [tolerance=±5% resistance=1M package=THT]
  P1 = Rotary Potentiometer (Large) [maximum_resistance=100kΩ package=THT]
  Rled = Resistor [tolerance=±5% resistance=470 package=THT]
  LED1 = LED - 5mm [color="Red (633nm)" package="5 mm [THT]"]

nets:
  enable: IC1.pin1, IC1.pin4, Rpulldown.Pin_1
  Din: IC1.pin2, P1.wiper
  Dout: IC1.pin3, Rled.Pin_0
  Cin: IC1.pin5
  Cout: IC1.pin6
  GND: IC1.pin7, IC1.pin9, IC1.pin10, IC1.pin12, IC1.pin13, V1.V-, Rpulldown.Pin_0, P1.leg1, LED1.cathode
  5V: IC1.pin14, V1.V+, P1.leg2
  N1: Rled.Pin_1, LED1.anode
