# Fritzing sketch APA102-Arduino (saved by Fritzing 0.9.4)

parts:
  APA102_LED_Strip1 = APA102 LED Strip [part_number=14015]
  Onderdeel1 = Arduino Uno (Rev3)

nets:
  GND: APA102_LED_Strip1.GND, Onderdeel1.GND
  N1: APA102_LED_Strip1.CI, Onderdeel1.D13/SCK
  N2: APA102_LED_Strip1.DI, Onderdeel1.D11_PWM/MOSI
  +5V: APA102_LED_Strip1.+5V, Onderdeel1.VIN

custom parts:
  APA102 LED Strip: APA102 LED strip, white, 60 LEDs/m
