# Fritzing sketch APA102-ESP32 (saved by Fritzing 0.9.4)
breadboards: 1

parts:
  IC1 = IC, DIP package, 30 pins [chip_label=ESP32]
  IC2 = IC, DIP package, 14 pins [chip_label=74AHCT126]
  APA102_LED_Strip1 = APA102 LED Strip [part_number=14015]

nets:
  N1: IC1.pin13, IC2.pin7, IC2.pin9, IC2.pin10, IC2.pin12, IC2.pin13, APA102_LED_Strip1.GND
  N2: IC1.pin14, IC2.pin1, IC2.pin4, IC2.pin14, APA102_LED_Strip1.+5V
  N3: IC1.pin26, IC2.pin5
  N4: IC1.pin27, IC2.pin2
  N5: IC2.pin3, APA102_LED_Strip1.DI
  N6: IC2.pin6, APA102_LED_Strip1.CI

custom parts:
  APA102 LED Strip: APA102 LED strip, white, 60 LEDs/m
