# Fritzing sketch pcb (saved by Fritzing 0.9.4)
circuit board: 6.11104cm x 4.56963cm
breadboards: 1

parts:
  J1 = female pin header, 18 pins [form="♀ (female)"]  # not connected
  J2 = female pin header, 24 pins [form="♀ (female)"]  # not connected
  ESP32-L = female pin header, 8 pins [form="♀ (female)"]
  ESP32-R = female pin header, 8 pins [form="♀ (female)"]
  IC1 = IC, DIP package, 14 pins [chip_label=IC]
  Q1 = Basic FET N-Channel [package="TO220 [THT]"]
  R1 = Resistor [tolerance=±5% resistance=220 package=THT]
  R2 = Resistor [tolerance=±5% resistance=220 package=THT]
  R3 = Resistor [tolerance=±5% resistance=220 package=THT]
  HALL = female pin header, 3 pins [form="♀ (female)"]
  APA102 = female pin header, 4 pins [form="♀ (female)"]
  C1 = Electrolytic Capacitor [capacitance=1µF package="100 mil [THT, electrolytic]"]
  C2 = Ceramic Capacitor [capacitance=200nF package="100 mil [THT, multilayer]"]
  C3 = Electrolytic Capacitor [capacitance=1µF package="100 mil [THT, electrolytic]"]

nets:
  GND: ESP32-L.pin6, IC1.pin7, IC1.pin9, IC1.pin10, IC1.pin12, IC1.pin13, Q1.source, R2.Pin_1, HALL.pin2, C2.1, C3.-
  5V: ESP32-L.pin7, IC1.pin14, HALL.pin1, APA102.pin4, C1.+, C2.0, C3.+
  GPIO16: ESP32-R.pin1, R3.Pin_0, HALL.pin3
  GPIO17: ESP32-R.pin2, IC1.pin1, IC1.pin4, R1.Pin_1
  GPIO18: ESP32-R.pin4, IC1.pin2
  GPIO23: ESP32-R.pin5, IC1.pin5
  3V3: ESP32-R.pin8, R3.Pin_1
  CI: IC1.pin3, APA102.pin3
  DI: IC1.pin6, APA102.pin2
  N1: Q1.gate, R1.Pin_0, R2.Pin_0
  ledGND: Q1.drain, APA102.pin1, C1.-
